# Fritzing sketch Blink (saved by Fritzing 0.9.2b)
breadboards: 1

parts:
  linino_one1 = linino one
  LED1 = LED - 5mm [color="Red (633nm)" package="5 mm [THT]"]
  R1 = Resistor [tolerance=±5% resistance=330 package=THT]

nets:
  N1: linino_one1.GND, R1.Pin_0
  N2: linino_one1.D12, LED1.anode
  N3: LED1.cathode, R1.Pin_1

notes:
  330Ω
