# Fritzing sketch DHT11 (saved by Fritzing 0.9.2b)
breadboards: 1

parts:
  linino_one1 = linino one
  DHT1 = DHT11 Humitidy and Temperature Sensor
  R1 = Resistor [tolerance=±5% resistance=220 package=THT]
  R2 = Resistor [tolerance=±5% resistance=220 package=THT]
  LED1 = LED - 5mm [color="Red (633nm)" package="5 mm [THT]"]
  S1 = Pushbutton [package="[THT]"]

nets:
  GND: linino_one1.GND, DHT1.GND, R2.Pin_0, S1.Pin_3, S1.Pin_4
  5V: linino_one1.5V, DHT1.VDD, R1.Pin_0
  N1: linino_one1.D2, DHT1.DATA, R1.Pin_1
  N2: linino_one1.D3, S1.Pin_1, S1.Pin_2
  N3: linino_one1.D12, LED1.anode
  N4: R2.Pin_1, LED1.cathode

notes:
  10kΩ
  330Ω

custom parts:
  DHT11 Humitidy and Temperature Sensor: DHT11 Humidity and Temperature Sensor
