# Fritzing sketch button (saved by Fritzing 0.9.2b)
breadboards: 1

parts:
  linino_one1 = linino one
  R2 = Resistor [tolerance=±5% resistance=220 package=THT]
  LED1 = LED - 5mm [color="Red (633nm)" package="5 mm [THT]"]
  S1 = Pushbutton [package="[THT]"]

nets:
  N1: linino_one1.GND, R2.Pin_0, S1.Pin_3, S1.Pin_4
  N2: linino_one1.D3, S1.Pin_1, S1.Pin_2
  N3: linino_one1.D12, LED1.anode
  N4: R2.Pin_1, LED1.cathode

notes:
  330Ω
